# Fritzing sketch lcd_spotify (saved by Fritzing 0.9.3b)

parts:
  S1 = Square Pushbutton
  Part1 = SparkFun Qwiic SHIM for Raspberry Pi [part_number="SparkFun #15794"]
  Part2 = LCD1602-I2C
  MCU1 = Raspberry Pi Zero

nets:
  GND: S1.leg0, Part1.GND, Part2.GND, MCU1.pin_6, MCU1.pin_9, MCU1.pin_39
  N1: S1.leg1, MCU1.pin_37
  VCC: Part1.VCC, Part2.VCC, MCU1.pin_1
  N2: Part1.SDA, Part2.SDA, MCU1.pin_3
  N3: Part1.SCL, Part2.SCL, MCU1.pin_5

custom parts:
  SparkFun Qwiic SHIM for Raspberry Pi: The SparkFun Qwiic SHIM for Raspberry Pi is a small, easily removable breakout that easily adds a Qwiic connector to your Raspberry Pi. The SHIM design allows you to plug directly to the Pi's I2C bus with no soldering required and the thin PCB design allows for it to be sandwiched on your Pi GPIO with other HATs! The Qwiic SHIM works great when you do not need the full capabilities of the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
  LCD1602-I2C: A standard character display, usually with 2x16 characters. Comes in many colors with LCM1602 IIC attached.
